# Fritzing sketch Lab3 (saved by Fritzing 0.9.4)
breadboards: 3

parts:
  U1 = 7427 3 x 3 Input NOR Gate [part_number=7427 package="DIP (Dual Inline) [THT]"]
  U2 = 74161 4 Bit Synchronous Up Down Counter [part_number=74161 package="DIP16 [THT]"]
  U3 = 7404 Hex Inverter [part_number=7404 package=dil14]
  U4 = 7474 Dual Positive Edge Triggered D Flip Flop [part_number=7474 package="DIP (Dual Inline) [THT]"]
  U5 = 7400 4 x 2 Input NAND Gate [part_number=7400 package="DIP (Dual Inline) [THT]"]
  A = 74194 4 Bit Bi-Directional Shift Register [part_number=74194 package="DIP16 [THT]"]
  B = 74194 4 Bit Bi-Directional Shift Register [part_number=74194 package="DIP16 [THT]"]
  U8 = 74157 Quad 2:1 MUX [part_number=74157 package="DIP16 [THT]"]
  U9 = 74153 Dual 4:1 MUX [part_number=74153 package="DIP16 [THT]"]
  U10 = 7400 4 x 2 Input NAND Gate [part_number=7400 package="DIP (Dual Inline) [THT]"]
  U11 = 7486 4 x 2 Input XOR Gate [part_number=7486 package="DIP (Dual Inline) [THT]"]
  U12 = 74157 Quad 2:1 MUX [part_number=74157 package="DIP16 [THT]"]
  U13 = 74153 Dual 4:1 MUX [part_number=74153 package="DIP16 [THT]"]

nets:
  N1: U1.A1, U2.15
  N2: U1.B1, U2.14
  GND: U1.GND, U2.1, U2.GND, U3.GND, U12.GND, U13.G1
  N3: U1.A4, U3.6A
  VCC: U1.VDD, U2.9, U2.VCC, U3.VCC, U4.A1, U4.Q2, U12.!STROBE, U12.VCC
  VCC_2: U2.7, A.VCC, B.VCC, U10.VDD, U11.VDD, U13.VCC
  N4: U3.1A, U9.Y1, U12.A3
  N5: U3.1Y, U12.B3
  N6: U3.4Y, U5.B1
  N7: U3.5Y, U5.A1
  N8: U3.5A, U4.A2, U8.SEL
  N9: U3.6Y, U4.B1
  GND_2: U4.GND, U5.GND, U8.GND, U8.A0, U9.G0, U9.GND
  VDD: U4.VDD, U5.VDD, U8.!STROBE, U8.VCC, U9.D1, U9.VCC
  N10: U5.Q1, A.9, B.9
  N11: U5.Q2, B.12, U10.A4, U10.B4, U11.B4, U13.C0, U13.A0, U13.D1
  N12: U5.A2, A.12, U10.B3, U10.Q3, U11.A4, U13.D0, U13.B1, U13.A1
  N13: U5.B2, U5.B3, U5.Q3
  N14: U5.A3, U9.A1
  N15: A.1, B.1
  N16: A.2, U13.Y1
  GND_3: A.GND, B.GND, U10.GND, U11.GND, U13.G0, U13.GND
  N17: A.10, B.10, U8.Y0
  N18: B.2, U13.Y0
  N19: U9.C1, U11.Q4
  N20: U9.B1, U10.Q1
  N21: U10.A1, U10.Q4
  N22: U10.B1, U10.A3
  N23: U12.Y3, U13.C1, U13.B0

notes:
  Execute
  LOAD A/B
  F1
  F0
  D3
  D2
  D0
  D1
  S1
  F2
  R0
  R1

custom parts:
  7427 3 x 3 Input NOR Gate: 7427 3 x 2 Input NOR Gate
  7404 Hex Inverter: 74XX04 Hex Inverter, Modified by Zuofu Cheng (Aug 2020)
  74157 Quad 2:1 MUX: 74157 Quad 2:1 Multiplexor
  74153 Dual 4:1 MUX: 74153 Dual 4:1 Multiplexor
